// Logisim project DecodeIR.circ as structural Verilog: 1 circuit, main circuit main
module DecodeIR (
  input  [31:0] IR,
  output WriteReg,
  output Store,
  output Load,
  output CTRL,
  output [2:0] GetOp,
  output [15:0] JMPAddress
);


  assign CTRL = 1'b0;
  assign GetOp = 3'b000;
  assign JMPAddress = {16{1'b0}};
  assign Load = 1'b0;
  assign Store = 1'b0;
  assign WriteReg = 1'b1;
endmodule
